// Logisim project trigges.circ as structural Verilog: 1 circuit, main circuit main
module main (
  input  not_S,
  input  R,
  input  not_R,
  input  S,
  input  S_2,
  input  C,
  input  R_2,
  input  not_S_2,
  input  S_3,
  input  C_2,
  input  R_3,
  input  not_R_2,
  input  D,
  input  C_3,
  input  not_S_3,
  input  not_S_4,
  input  C_4,
  input  C_5,
  input  not_R_3,
  input  not_R_4,
  input  not_S_5,
  input  T,
  input  not_R_5,
  input  not_S_6,
  input  J,
  input  C_6,
  input  K,
  input  not_R_6,
  output Q,
  output Q_2,
  output not_Q,
  output not_Q_2,
  output Q_3,
  output not_Q_3,
  output Q_4,
  output not_Q_4,
  output Q_5,
  output not_Q_5,
  output Q_6,
  output Q_7,
  output not_Q_6,
  output not_Q_7,
  output Q_8,
  output not_Q_8,
  output Q_9,
  output not_Q_9
);

  wire C_2_out, nand_3_out, nand_4_out, nand_5_out, nand_6_out, nand_7_out, nand_8_out, nand_9_out,
       nand_12_out, nand_13_out, nand_14_out, nand_15_out, nand_16_out, nand_17_out, nand_18_out,
       nand_19_out, nand_20_out, nand_21_out, nand_22_out, nand_27_out, nand_28_out, nand_29_out,
       nand_30_out, nand_31_out, nand_32_out, nand_33_out, nand_34_out, nand_35_out, nand_36_out, nor_3_out,
       nor_4_out, nor_5_out, nor_6_out;

  Clock u_C ();  // open: out
  nand nand_1 (Q, not_S, not_Q);
  nand nand_2 (not_Q, Q, not_R);
  Clock u_C_2 (.out(C_2_out));
  nand nand_3 (nand_3_out, not_S_3, nand_6_out);
  nand nand_4 (nand_4_out, nand_7_out, not_R_3);
  Clock u_T ();  // open: out
  nand nand_5 (nand_5_out, C_2_out, C_2_out);
  nand nand_6 (nand_6_out, nand_7_out, nand_3_out, C_4);
  nand nand_7 (nand_7_out, C_4, nand_4_out, nand_6_out);
  nand nand_8 (nand_8_out, S_3, nand_5_out);
  nand nand_9 (nand_9_out, nand_5_out, R_3);
  nand nand_10 (Q_6, nand_6_out, not_Q_6);
  nand nand_11 (not_Q_6, Q_6, nand_7_out);
  nand nand_12 (nand_12_out, T, T);
  nand nand_13 (nand_13_out, not_Q_9, J, C_6);
  nand nand_14 (nand_14_out, C_6, K, Q_9);
  nand nand_15 (nand_15_out, S_2, C);
  nand nand_16 (nand_16_out, C, R_2);
  nand nand_17 (nand_17_out, not_S_2, nand_8_out, nand_18_out);
  nand nand_18 (nand_18_out, nand_17_out, nand_9_out, not_R_2);
  nand nand_19 (nand_19_out, D, C_3);
  nand nand_20 (nand_20_out, C_3, nand_19_out);
  nand nand_21 (nand_21_out, not_Q_8, nand_12_out);
  nand nand_22 (nand_22_out, nand_12_out, Q_8);
  nand nand_23 (Q_3, nand_15_out, not_Q_3);
  nand nand_24 (not_Q_3, Q_3, nand_16_out);
  nand nand_25 (Q_5, nand_19_out, not_Q_5);
  nand nand_26 (not_Q_5, Q_5, nand_20_out);
  nand nand_27 (nand_27_out, not_S_5, nand_21_out, nand_28_out);
  nand nand_28 (nand_28_out, nand_27_out, nand_22_out, not_R_5);
  nand nand_29 (nand_29_out, not_S_6, nand_13_out, nand_30_out);
  nand nand_30 (nand_30_out, nand_29_out, nand_14_out, not_R_6);
  nand nand_31 (nand_31_out, nand_17_out, C_2_out);
  nand nand_32 (nand_32_out, C_2_out, nand_18_out);
  nand nand_33 (nand_33_out, nand_27_out, T);
  nand nand_34 (nand_34_out, T, nand_28_out);
  nand nand_35 (nand_35_out, nand_29_out, nand_13_out, nand_14_out);
  nand nand_36 (nand_36_out, nand_14_out, nand_13_out, nand_30_out);
  nand nand_37 (Q_4, not_S_2, nand_31_out, not_Q_4);
  nand nand_38 (not_Q_4, Q_4, nand_32_out, not_R_2);
  nand nand_39 (Q_8, not_S_5, nand_33_out, not_Q_8);
  nand nand_40 (not_Q_8, Q_8, nand_34_out, not_R_5);
  nand nand_41 (Q_9, not_S_6, not_Q_9, nand_35_out);
  nand nand_42 (not_Q_9, nand_36_out, Q_9, not_R_6);
  nor nor_1 (Q_2, R, not_Q_2);
  nor nor_2 (not_Q_2, Q_2, S);
  nor nor_3 (nor_3_out, not_S_4, nor_4_out);
  nor nor_4 (nor_4_out, nor_5_out, nor_3_out, C_5);
  nor nor_5 (nor_5_out, C_5, nor_6_out, nor_4_out);
  nor nor_6 (nor_6_out, nor_5_out, not_R_4);
  nor nor_7 (Q_7, nor_4_out, not_Q_7);
  nor nor_8 (not_Q_7, Q_7, nor_5_out);
endmodule
